// Logisim project 3 to 8 decoder (nand).circ as structural Verilog: 1 circuit, main circuit main
module main (
  input  E,
  input  A,
  input  B,
  input  C,
  output d0,
  output d1,
  output d2,
  output d3,
  output d4,
  output d5,
  output d6,
  output d7
);

  wire not_1_out, not_2_out, not_3_out, not_4_out;

  not not_1 (not_1_out, A);
  not not_2 (not_2_out, B);
  not not_3 (not_3_out, E);
  not not_4 (not_4_out, C);
  nand nand_1 (d0, not_1_out, not_2_out, not_3_out, not_4_out);
  nand nand_2 (d1, not_1_out, not_2_out, C, not_3_out);
  nand nand_3 (d2, not_1_out, B, not_4_out, not_3_out);
  nand nand_4 (d3, not_1_out, B, C, not_3_out);
  nand nand_5 (d4, A, not_2_out, not_4_out, not_3_out);
  nand nand_6 (d5, A, not_2_out, C, not_3_out);
  nand nand_7 (d6, A, B, not_4_out, not_3_out);
  nand nand_8 (d7, A, B, C, not_3_out);
endmodule
