// Logisim project 3 to 8 decoder.circ as structural Verilog: 1 circuit, main circuit main
module main (
  input  A,
  input  B,
  input  C,
  input  E,
  output S,
  output C_2
);

  wire and_1_out, and_2_out, and_3_out, and_4_out, and_5_out, and_6_out, and_7_out, and_8_out, not_1_out,
       not_2_out, not_3_out;

  not not_1 (not_1_out, A);
  not not_2 (not_2_out, B);
  not not_3 (not_3_out, C);
  and and_1 (and_1_out, not_1_out, not_2_out, E, not_3_out);
  and and_2 (and_2_out, not_1_out, not_2_out, C, E);
  and and_3 (and_3_out, not_1_out, B, not_3_out, E);
  and and_4 (and_4_out, not_1_out, B, C, E);
  and and_5 (and_5_out, A, not_2_out, not_3_out, E);
  and and_6 (and_6_out, A, not_2_out, C, E);
  and and_7 (and_7_out, A, B, not_3_out, E);
  and and_8 (and_8_out, A, B, C, E);
  or or_1 (S, and_2_out, and_3_out, and_5_out, and_8_out);
  or or_2 (C_2, and_4_out, and_6_out, and_7_out, and_8_out);

  // Notes on the sheet:
  //   s=1,2,4,7
  //   c=3,5,6,7
  //   Half Adder using 3 to 8 decoder
endmodule
