// Logisim project 4 to 2 Priority Encoder.circ as structural Verilog: 1 circuit, main circuit main
module main (
  input  I1,
  input  I2,
  input  I3,
  output Y0,
  output Y1
);

  wire and_1_out, not_1_out;

  not not_1 (not_1_out, I2);
  and and_1 (and_1_out, I1, not_1_out);
  or or_1 (Y1, I2, I3);
  or or_2 (Y0, and_1_out, I3);

  // Notes on the sheet:
  //   4 to 2 Priority Encoder
endmodule
