// Logisim project 8 to 3 multiplexer.circ as structural Verilog: 1 circuit, main circuit main
module main (
  input  s2,
  input  d1,
  input  d0,
  input  d0_2,
  input  d1_2,
  input  d2,
  input  d3,
  input  d4,
  input  d5,
  input  d6,
  input  d7,
  output Z
);

  wire and_1_out, and_2_out, and_3_out, and_4_out, and_5_out, and_6_out, and_7_out, and_8_out, not_1_out,
       not_2_out, not_3_out;

  not not_1 (not_1_out, d1);
  not not_2 (not_2_out, s2);
  not not_3 (not_3_out, d0);
  and and_1 (and_1_out, d0_2, not_2_out, not_1_out, not_3_out);
  and and_2 (and_2_out, d1_2, not_2_out, not_1_out, d0);
  and and_3 (and_3_out, d2, not_2_out, d1, not_3_out);
  and and_4 (and_4_out, d3, not_2_out, d1, d0);
  and and_5 (and_5_out, d4, s2, not_1_out, not_3_out);
  and and_6 (and_6_out, d5, s2, not_1_out, d0);
  and and_7 (and_7_out, d6, s2, d1, not_3_out);
  and and_8 (and_8_out, d7, s2, d1, d0);
  or or_1 (Z, and_1_out, and_2_out, and_3_out, and_4_out, and_5_out, and_6_out, and_7_out, and_8_out);

  // Notes on the sheet:
  //   Logic Diagram of 8 to 3 Multiplexer
endmodule
