// Logisim project Half Adder using 3 to 8 decoder.circ as structural Verilog: 1 circuit, main circuit main
module main (
  input  A,
  input  B,
  input  C,
  input  E,
  output d0,
  output d1,
  output d2,
  output d3,
  output d4,
  output d5,
  output d6,
  output d7
);

  wire not_1_out, not_2_out, not_3_out;

  not not_1 (not_1_out, A);
  not not_2 (not_2_out, B);
  not not_3 (not_3_out, C);
  and and_1 (d0, not_1_out, not_2_out, E, not_3_out);
  and and_2 (d1, not_1_out, not_2_out, C, E);
  and and_3 (d2, not_1_out, B, not_3_out, E);
  and and_4 (d3, not_1_out, B, C, E);
  and and_5 (d4, A, not_2_out, not_3_out, E);
  and and_6 (d5, A, not_2_out, C, E);
  and and_7 (d6, A, B, not_3_out, E);
  and and_8 (d7, A, B, C, E);
endmodule
