// Logisim project Logic Circuit for 2 bit Comparator.circ as structural Verilog: 1 circuit, main circuit main
module main (
  input  a1,
  input  a0,
  input  b1,
  input  b0,
  output G,
  output E,
  output L
);

  wire and_1_out, and_2_out, and_3_out, and_4_out, and_5_out, and_6_out, not_1_out, not_2_out, not_3_out,
       not_4_out, xnor_1_out, xnor_2_out;

  not not_1 (not_1_out, b1);
  not not_2 (not_2_out, b0);
  not not_3 (not_3_out, a1);
  not not_4 (not_4_out, a0);
  and and_1 (and_1_out, a1, not_1_out);
  and and_2 (and_2_out, a0, not_1_out, not_2_out);
  and and_3 (and_3_out, a1, a0, not_2_out);
  xnor xnor_1 (xnor_1_out, a0, b0);
  xnor xnor_2 (xnor_2_out, a1, b1);
  and and_4 (and_4_out, not_3_out, b1);
  and and_5 (and_5_out, not_3_out, not_4_out, b0);
  and and_6 (and_6_out, not_4_out, b1, b0);
  and and_7 (E, xnor_1_out, xnor_2_out);
  or or_1 (L, and_4_out, and_5_out, and_6_out);
  or or_2 (G, and_1_out, and_2_out, and_3_out);

  // Notes on the sheet:
  //   Logic Circuit for 2- Bit Comparator
endmodule
